# Fritzing sketch bumper (saved by Fritzing 0.9.3b)
breadboards: 1

parts:
  Part2 = Arduino Uno (Rev3)
  R2 = Resistor [tolerance=±5% resistance=220 package="2010 [SMD]"]
  S1 = Round Pushbutton

nets:
  N1: Part2.D8, R2.Pin_0, S1.leg0
  N2: Part2.5V, S1.leg1
  N3: Part2.GND, R2.Pin_1

notes:
  Se establecen las entradas de 5V y GND.
  Se selecciona un entrada de datos. En este caso el 8.
