# Fritzing sketch button (saved by Fritzing 0.9.3b)
breadboards: 1

parts:
  R4 = Resistor [tolerance=±5% resistance=220 package="2512 [SMD]"]
  S1 = Momentary Switch [package=ksa_sealed_tac_switch]
  Part1 = Arduino Uno (Rev3) - ICSP

nets:
  N1: R4.Pin_0, Part1.GND
  N2: R4.Pin_1, S1.4, Part1.D2
  N3: S1.2, Part1.5V

notes:
  El boton necesita dos entradas, la entrada de 5V y la entrada de GND.
  Ademas necesita otra entrada digital. En este caso es el numero 2.
  Tambien se necesita una resistencia que tengan ese orden de colores.
