# Fritzing sketch buzzer-2 (saved by Fritzing 0.9.3b)
breadboards: 1

parts:
  Part6 = Arduino Uno (Rev3)
  J1 = Piezo Speaker

nets:
  N1: Part6.GND, J1.pin1
  N2: Part6.D3_PWM, J1.pin2

notes:
  Se seleccionan entrada para GND y para datos que en este caso es la ~3.
