# Fritzing sketch buzzer (saved by Fritzing 0.9.3b)

parts:
  Part5 = Arduino Uno (Rev3)
  J1 = Piezo Speaker

nets:
  N1: Part5.D3_PWM, J1.pin2

notes:
  Se seleccionan entrada para GND y para datos que en este caso es la ~3.
