# Fritzing sketch button-bumper-switch (saved by Fritzing 0.9.3b)
breadboards: 1

parts:
  Part3 = Arduino Uno (Rev3)
  R3 = Resistor [tolerance=±5% resistance=220 package="2010 [SMD]"]
  S2 = Round Pushbutton
  R4 = Resistor [tolerance=±5% resistance=220 package="2010 [SMD]"]
  S3 = Toggle Switch [package=THT]  # not connected
  S4 = Pushbutton [package="[SMD]"]  # not connected

nets:
  N1: Part3.D8, R3.Pin_0, S2.leg0
  N2: Part3.D2, R4.Pin_0
  N3: Part3.5V, S2.leg1, R4.Pin_1
  N4: Part3.GND, R3.Pin_1

notes:
  Es la misma conexion para un interruptor como para un pulsador.
