# Fritzing sketch joystick (saved by Fritzing 0.9.3b)
breadboards: 1

parts:
  Part3 = Arduino Uno (Rev3)
  Part4 = Thumb Joystick

nets:
  N1: Part3.A0, Part4.VERT
  N2: Part3.A1, Part4.HORZ
  5V: Part3.5V, Part4.VCC
  GND: Part3.GND, Part4.GND
