# Fritzing sketch led-rgb-2 (saved by Fritzing 0.9.3b)
breadboards: 1

parts:
  Part2 = Arduino Uno (Rev3) - ICSP
  LED3 = RGB LED (com. cathode, rgb) [package="5 mm [THT]"]

nets:
  N1: Part2.GND, LED3.common_cathode
  N2: Part2.D3_PWM, LED3.blue_anode
  N3: Part2.D5_PWM, LED3.green_anode
  N4: Part2.D6_PWM, LED3.red_anode

notes:
  La entrada GND se simboliza con el cable negro.
  La entrada de los colores primarios estan simbolizados por las entradas 3,5 y 6.
