# Fritzing sketch led-rgb (saved by Fritzing 0.9.3b)
breadboards: 1

parts:
  Part1 = Arduino Uno (Rev3) - ICSP
  LED1 = RGB LED (com. cathode, rgb) [package="5 mm [THT]"]

nets:
  N1: Part1.GND, LED1.common_cathode
  N2: Part1.D3_PWM, LED1.blue_anode
  N3: Part1.D5_PWM, LED1.green_anode
  N4: Part1.D6_PWM, LED1.red_anode

notes:
  La entrada GND se simboliza con el cable negro.
  La entrada de los colores primarios estan simbolizados por las entradas 3,5 y 6.
