# Fritzing sketch led (saved by Fritzing 0.9.3b)
breadboards: 1

parts:
  Part1 = Arduino Uno (Rev3)
  LED1 = LED - 5mm [color="Red (633nm)" package="5 mm [THT]"]

nets:
  N1: Part1.D13/SCK, LED1.cathode
  N2: Part1.GND, LED1.anode

notes:
  GND: Representa la entrada de energia a la placa Arduino UNO.
  Pin 13: La entrada del pin 13 hace referencia a la entrada de datos definido en la variable definida para el led.
