# Fritzing sketch motors (saved by Fritzing 0.9.3b)
breadboards: 1

parts:
  M1 = DC Motor
  Part1 = Arduino Uno (Rev3)
  Q1 = PNP-Transistor [package="TO92 [THT]"]
  D1 = Rectifier Diode [part_number=1N4001 package="Melf DO-213 AB [SMD]"]
  R1 = Resistor [tolerance=±5% resistance=220 package=THT]

nets:
  N1: M1.pin_1, Q1.C, D1.anode
  N2: M1.pin_2, D1.cathode
  N3: Part1.GND, Q1.E
  N4: Q1.B, R1.Pin_1
