# Fritzing sketch potentiometer (saved by Fritzing 0.9.3b)
breadboards: 1

parts:
  Part1 = Arduino Uno (Rev3)
  U1 = POT [package=pot_mammoth]

nets:
  N1: Part1.A3, U1.A
  N2: Part1.5V, U1.E
  N3: Part1.GND, U1.S
