# Fritzing sketch proximity-board (saved by Fritzing 0.9.3b)
breadboards: 1

parts:
  Part2 = Arduino Uno (Rev3)
  J1 = Infrared Proximity Sensor

nets:
  N1: Part2.A0, J1.Vout
  5V: Part2.5V, J1.Vcc
  GND: Part2.GND, J1.GND
