# Fritzing sketch servomotors-2 (saved by Fritzing 0.9.3b)

parts:
  Part8 = Arduino Uno (Rev3)
  J2 = Basic Servo

nets:
  N1: Part8.D10_PWM/SS, J2.pulse
  5V: Part8.5V, J2.vcc
  GND: Part8.GND, J2.gnd
