# Fritzing sketch servomotors (saved by Fritzing 0.9.3b)
breadboards: 1

parts:
  Part7 = Arduino Uno (Rev3)
  J1 = Basic Servo

nets:
  N1: Part7.D10_PWM/SS, J1.pulse
  5V: Part7.5V, J1.vcc
  GND: Part7.GND, J1.gnd
