# Fritzing sketch switch (saved by Fritzing 0.9.3b)
breadboards: 1

parts:
  S1 = Toggle Switch [package=THT]
  Part1 = Arduino Uno (Rev3)
  R1 = Resistor [tolerance=±5% resistance=220 package="2010 [SMD]"]

nets:
  N1: S1.L1, Part1.D8, R1.Pin_0
  N2: S1.COM, S1.L2, Part1.5V
  N3: Part1.GND, R1.Pin_1
